// Logisim project exercice1.circ as structural Verilog
module exercice1 (
  input  A,
  input  B,
  output S
);

  wire and_1_out, and_2_out, not_1_out;

  not not_1 (not_1_out, A);
  and and_1 (and_1_out, A, B);
  and and_2 (and_2_out, B, not_1_out);
  or or_1 (S, and_1_out, and_2_out);
endmodule

module exercice2 (
  input  I0,
  input  I1,
  input  I2,
  output zero,
  output un,
  output deux,
  output trois,
  output quatre,
  output cinq,
  output six,
  output sept
);

  wire not_1_out, not_2_out, not_3_out;

  // AND_Gate and_1 is placed but not wired
  not not_1 (not_1_out, I0);
  not not_2 (not_2_out, I1);
  not not_3 (not_3_out, I2);
  and and_2 (zero, not_1_out, not_2_out, not_3_out);
  and and_3 (un, I0, not_2_out, not_3_out);
  and and_4 (deux, not_1_out, I1, not_3_out);
  and and_5 (trois, I0, I1, not_3_out);
  // AND_Gate and_6 is placed but not wired
  and and_7 (quatre, not_1_out, not_2_out, I2);
  and and_8 (cinq, I0, not_2_out, I2);
  and and_9 (six, not_1_out, I1, I2);
  and and_10 (sept, I2, I1, I0);
endmodule

module exercice03 (
  input  I0,
  input  I1,
  input  I2
);

  wire exercice2_1_cinq, exercice2_1_deux, exercice2_1_quatre, exercice2_1_sept, exercice2_1_six,
       exercice2_1_trois, exercice2_1_un, exercice2_1_zero, or_1_out, or_2_out, or_3_out, or_4_out, or_5_out,
       or_6_out, or_7_out;

  exercice2 exercice2_1 (
    .I0(I0), .I1(I1), .I2(I2), .zero(exercice2_1_zero), .un(exercice2_1_un), .deux(exercice2_1_deux),
    .trois(exercice2_1_trois), .quatre(exercice2_1_quatre), .cinq(exercice2_1_cinq), .six(exercice2_1_six),
    .sept(exercice2_1_sept));
  or or_1 (or_1_out, exercice2_1_six, exercice2_1_deux, exercice2_1_trois, exercice2_1_quatre, exercice2_1_cinq);
  or or_2 (or_2_out, exercice2_1_zero, exercice2_1_quatre, exercice2_1_cinq, exercice2_1_six);
  _7_Segment_Display #(.decimalPoint("false")) u_7_segment_display_1 (
    .g(or_1_out), .f(or_2_out), .a(or_3_out), .b(or_4_out), .e(or_5_out), .d(or_6_out), .c(or_7_out));
  or or_3 (or_3_out, exercice2_1_zero, exercice2_1_deux, exercice2_1_trois, exercice2_1_cinq, exercice2_1_six, exercice2_1_sept);
  or or_4 (or_4_out, exercice2_1_zero, exercice2_1_un, exercice2_1_deux, exercice2_1_trois, exercice2_1_quatre, exercice2_1_sept);
  or or_5 (or_5_out, exercice2_1_zero, exercice2_1_deux, exercice2_1_six);
  or or_6 (or_6_out, exercice2_1_zero, exercice2_1_deux, exercice2_1_trois, exercice2_1_cinq, exercice2_1_six);
  or or_7 (or_7_out, exercice2_1_zero, exercice2_1_un, exercice2_1_trois, exercice2_1_quatre, exercice2_1_cinq, exercice2_1_six, exercice2_1_sept);
endmodule

module exercice04 (
  input  A,
  input  B,
  output eg,
  output sup,
  output inf
);

  wire not_1_out, not_2_out;

  xnor xnor_1 (eg, A, B);
  not not_1 (not_1_out, B);
  and and_1 (sup, A, not_1_out);
  not not_2 (not_2_out, A);
  and and_2 (inf, not_2_out, B);
endmodule

module exercice05 (
  input  [3:0] A,
  input  [3:0] B,
  output eg,
  output Sup
);

  wire and_2_out, and_3_out, and_4_out, exercice04_1_eg, exercice04_1_inf, exercice04_1_sup, exercice04_2_eg,
       exercice04_2_inf, exercice04_2_sup, exercice04_3_eg, exercice04_3_inf, exercice04_3_sup,
       exercice04_4_eg, exercice04_4_inf, exercice04_4_sup;

  exercice04 exercice04_1 (.A(B[0]), .B(A[0]), .eg(exercice04_1_eg), .sup(exercice04_1_sup), .inf(exercice04_1_inf));
  exercice04 exercice04_2 (.A(B[1]), .B(A[1]), .eg(exercice04_2_eg), .sup(exercice04_2_sup), .inf(exercice04_2_inf));
  exercice04 exercice04_3 (.A(B[2]), .B(A[2]), .eg(exercice04_3_eg), .sup(exercice04_3_sup), .inf(exercice04_3_inf));
  exercice04 exercice04_4 (.A(B[3]), .B(A[3]), .eg(exercice04_4_eg), .sup(exercice04_4_sup), .inf(exercice04_4_inf));
  and and_1 (eg, exercice04_1_eg, exercice04_2_eg, exercice04_3_eg, exercice04_4_eg);
  and and_2 (and_2_out, exercice04_4_eg, exercice04_3_sup);
  and and_3 (and_3_out, exercice04_4_eg, exercice04_3_eg, exercice04_2_sup);
  and and_4 (and_4_out, exercice04_4_eg, exercice04_3_eg, exercice04_2_eg, exercice04_1_sup);
  or or_1 (Sup, and_2_out, and_3_out, and_4_out, exercice04_4_sup);
endmodule
