// Logisim project partie2_r103_tp(1).circ as structural Verilog: 5 circuits, main circuit main
module main (
  input  A,
  input  B,
  input  C,
  output P,
  output G,
  output S
);

  wire xor_1_out;

  xor xor_1 (xor_1_out, A, B);
  xor xor_2 (S, xor_1_out, C);
  or or_1 (P, A, B);
  and and_1 (G, A, B);
endmodule

module parte2_2 (
  input  G0,
  input  P0,
  input  C0,
  output C1
);

  wire and_1_out;

  and and_1 (and_1_out, P0, C0);
  or or_1 (C1, G0, and_1_out);
endmodule

module parte2_3 (
  input  C0,
  input  P0,
  input  P1,
  input  G0,
  input  G1,
  output C2
);

  wire and_1_out, and_2_out;

  and and_1 (and_1_out, C0, P0, P1);
  and and_2 (and_2_out, P1, G0);
  or or_1 (C2, and_1_out, and_2_out, G1);
endmodule

module parte2_4 (
  input  C0,
  input  P0,
  input  P1,
  input  P2,
  input  P3,
  input  G3,
  input  G2,
  input  G1,
  input  G0,
  output C1,
  output C2,
  output C3,
  output C4
);

  wire and_1_out, and_2_out, and_3_out, and_4_out, and_5_out, and_6_out, and_7_out, and_8_out, and_9_out,
       and_10_out;

  and and_1 (and_1_out, C0, P0);
  or or_1 (C1, and_1_out, G0);
  and and_2 (and_2_out, C0, P0, P1);
  and and_3 (and_3_out, P1, G0);
  or or_2 (C2, and_2_out, and_3_out, G1);
  and and_4 (and_4_out, C0, P0, P1, P2);
  and and_5 (and_5_out, P1, P2, G0);
  or or_3 (C3, and_4_out, and_5_out, and_6_out, G2);
  and and_6 (and_6_out, P2, G1);
  and and_7 (and_7_out, G0, P3, P2, P1, P0);
  and and_8 (and_8_out, G1, P3, P2, P1);
  and and_9 (and_9_out, G2, P2, P3);
  and and_10 (and_10_out, P3, G2);
  or or_4 (C4, and_7_out, and_8_out, and_9_out, and_10_out, G3);
endmodule

module PARTE2_5 (
  input  [3:0] in_1,
  input  [3:0] in_2,
  input  in_3,
  output out_4,
  output out_5,
  output out_6,
  output out_7,
  output out_8
);

  wire main_1_g, main_1_p, main_2_g, main_2_p, main_3_g, main_3_p, main_4_g, main_4_p, parte2_4_1_c1,
       parte2_4_1_c2, parte2_4_1_c3;

  main main_1 (.A(in_1[0]), .B(in_2[0]), .C(in_3), .P(main_1_p), .G(main_1_g), .S(out_4));
  main main_2 (.A(in_1[1]), .B(in_2[1]), .C(parte2_4_1_c1), .P(main_2_p), .G(main_2_g), .S(out_5));
  main main_3 (.A(in_1[2]), .B(in_2[2]), .C(parte2_4_1_c2), .P(main_3_p), .G(main_3_g), .S(out_6));
  main main_4 (.A(in_1[3]), .B(in_2[3]), .C(parte2_4_1_c3), .P(main_4_p), .G(main_4_g), .S(out_7));
  parte2_4 parte2_4_1 (
    .C0(in_3), .P0(main_1_p), .P1(main_2_p), .P2(main_3_p), .P3(main_4_p), .G3(main_1_g), .G2(main_2_g),
    .G1(main_3_g), .G0(main_4_g), .C1(parte2_4_1_c1), .C2(parte2_4_1_c2), .C3(parte2_4_1_c3), .C4(out_8));
endmodule
