// Logisim project prendbits4.circ as structural Verilog: 8 circuits, main circuit main
module main (
  input  [1:0] in_1,
  input  in_2,
  output out_3,
  output out_4
);

  and and_1 (out_3, in_1[0], in_2);
  xor xor_1 (out_4, in_1[0], in_2);
  // Pins of 1 and 2 bits meet at in_1
endmodule

module E2 (
  input  A,
  input  B,
  input  C,
  output s1,
  output S0
);

  wire and_1_out, and_2_out, xor_1_out;

  and and_1 (and_1_out, A, B);
  xor xor_1 (xor_1_out, A, B);
  xor xor_2 (S0, xor_1_out, C);
  and and_2 (and_2_out, C, xor_1_out);
  or or_1 (s1, and_1_out, and_2_out);
endmodule

module E3 (
  input  in_1,
  input  [1:0] A,
  input  [1:0] B,
  output S0,
  output S1,
  output S2
);

  wire e2_1_s1;

  E2 e2_1 (.A(A[0]), .B(B[0]), .C(in_1), .s1(e2_1_s1), .S0(S0));
  E2 e2_2 (.A(A[1]), .B(B[1]), .C(e2_1_s1), .s1(S2), .S0(S1));
endmodule

module bits4 (
  input  [3:0] in_1,
  input  [3:0] in_2,
  input  in_3,
  output c,
  output S3,
  output S2,
  output [3:0] out_7,
  output S1,
  output s0
);

  wire e2_1_s1, e2_2_s1, e2_3_s1;

  E2 e2_1 (.A(in_1[0]), .B(in_2[0]), .C(in_3), .s1(e2_1_s1), .S0(out_7[0]));
  E2 e2_2 (.A(in_1[1]), .B(in_2[1]), .C(e2_1_s1), .s1(e2_2_s1), .S0(out_7[1]));
  E2 e2_3 (.A(in_1[2]), .B(in_2[2]), .C(e2_2_s1), .s1(e2_3_s1), .S0(out_7[2]));
  E2 e2_4 (.A(in_1[3]), .B(in_2[3]), .C(e2_3_s1), .s1(c), .S0(out_7[3]));

  assign s0 = out_7[0];
  assign S1 = out_7[1];
  assign S2 = out_7[2];
  assign S3 = out_7[3];
endmodule

module bit16 (
  input  [15:0] in_1,
  input  [15:0] in_2,
  input  [3:0] in_3,
  input  [3:0] tamer
);

  unitecalcul unitecalcul_1 ();  // open: C0, P0, P1, P2, P3, G3, G2, G1, G0, C1, C2, C3, C4, SG, SP
  bits4 bits4_1 ();  // open: in_1, in_2, in_3, c, S3, S2, out_7, S1, s0
  bits4 bits4_2 ();  // open: in_1, in_2, in_3, c, S3, S2, out_7, S1, s0
  bits4 bits4_3 ();  // open: in_1, in_2, in_3, c, S3, S2, out_7, S1, s0
  bits4 bits4_4 ();  // open: in_1, in_2, in_3, c, S3, S2, out_7, S1, s0
endmodule

module unitecalculv2 (
  input  C0,
  input  P0,
  input  P1,
  input  P2,
  input  P3,
  input  G3,
  input  G2,
  input  G1,
  output C1,
  output C2,
  output C3,
  output C4
);

  wire and_1_out, and_2_out, and_3_out, and_4_out, and_5_out, and_6_out, and_7_out, and_8_out, and_9_out,
       and_10_out, undriven;

  and and_1 (and_1_out, C0, P0);
  or or_1 (C1, and_1_out, undriven);
  and and_2 (and_2_out, C0, P0, P1);
  and and_3 (and_3_out, P1, undriven);
  or or_2 (C2, and_2_out, and_3_out, G1);
  and and_4 (and_4_out, C0, P0, P1, P2);
  and and_5 (and_5_out, P1, P2, undriven);
  or or_3 (C3, and_4_out, and_5_out, and_6_out, G2);
  and and_6 (and_6_out, P2, G1);
  and and_7 (and_7_out, undriven, P3, P2, P1, P0);
  and and_8 (and_8_out, G1, P3, P2, P1);
  and and_9 (and_9_out, G2, P2, P3);
  and and_10 (and_10_out, P3, G2);
  or or_4 (C4, and_7_out, and_8_out, and_9_out, and_10_out, G3);
endmodule

module main2 (
  input  A,
  input  B,
  input  C,
  output P,
  output G,
  output S
);

  wire xor_1_out;

  xor xor_1 (xor_1_out, A, B);
  xor xor_2 (S, xor_1_out, C);
  or or_1 (P, A, B);
  and and_1 (G, A, B);
endmodule

module unitecalcul (
  input  C0,
  input  P0,
  input  P1,
  input  P2,
  input  P3,
  input  G3,
  input  G2,
  input  G1,
  input  G0,
  output C1,
  output C2,
  output C3,
  output C4,
  output SG,
  output SP
);

  wire and_1_out, and_2_out, and_3_out, and_4_out, and_5_out, and_6_out, and_7_out, and_8_out, and_9_out,
       and_10_out, and_12_out, and_13_out, and_14_out;

  and and_1 (and_1_out, C0, P0);
  or or_1 (C1, and_1_out, G0);
  and and_2 (and_2_out, C0, P0, P1);
  and and_3 (and_3_out, P1, G0);
  or or_2 (C2, and_2_out, and_3_out, G1);
  and and_4 (and_4_out, C0, P0, P1, P2);
  and and_5 (and_5_out, P1, P2, G0);
  or or_3 (C3, and_4_out, and_5_out, and_6_out, G2);
  and and_6 (and_6_out, P2, G1);
  and and_7 (and_7_out, G0, P3, P2, P1, P0);
  and and_8 (and_8_out, G1, P3, P2, P1);
  and and_9 (and_9_out, G2, P2, P3);
  and and_10 (and_10_out, P3, G2);
  or or_4 (C4, and_7_out, and_8_out, and_9_out, and_10_out, G3);
  and and_11 (SP, P0, P1, P2, P3);
  and and_12 (and_12_out, G0, P1, P2, P3);
  and and_13 (and_13_out, G1, P2, P3);
  or or_5 (SG, and_12_out, and_13_out, and_14_out, G3);
  and and_14 (and_14_out, G2, P3);
endmodule
