// Logisim project tdlogisim.circ as structural Verilog: 4 circuits, main circuit main
module main (
  input  a,
  input  b,
  input  c,
  input  d,
  input  in_5,
  input  in_6,
  output out_7
);

  wire multiplexer_1_out, multiplexer_2_out;

  Multiplexer multiplexer_1 (.in0(a), .in1(b), .out(multiplexer_1_out), .sel(in_5));
  Multiplexer multiplexer_2 (.in0(c), .in1(d), .out(multiplexer_2_out), .sel(in_5));
  Multiplexer multiplexer_3 (.in0(multiplexer_1_out), .in1(multiplexer_2_out), .out(out_7), .sel(in_6));
endmodule

module mux (
  input  in_1,
  input  in_2,
  input  in_3,
  input  in_4,
  input  in_5,
  input  in_6,
  output out_7
);

  wire and_1_out, and_2_out, and_3_out, and_4_out, and_5_out, and_6_out, not_1_out, not_2_out, or_1_out,
       or_2_out;

  not not_1 (not_1_out, in_4);
  and and_1 (and_1_out, in_3, in_4);
  and and_2 (and_2_out, in_4, in_4);
  and and_3 (and_3_out, in_2, not_1_out);
  and and_4 (and_4_out, in_6, not_1_out);
  or or_1 (or_1_out, and_3_out, and_1_out);
  or or_2 (or_2_out, and_2_out, and_4_out);
  not not_2 (not_2_out, in_1);
  and and_5 (and_5_out, or_1_out, not_2_out);
  and and_6 (and_6_out, or_2_out, in_1);
  or or_3 (out_7, and_5_out, and_6_out);

  assign in_5 = in_4;
endmodule

module ex4 (
  input  in_1,
  input  in_2,
  output out_3,
  output out_4
);

  wire not_1_out;

  and and_1 (out_3, in_1, not_1_out);
  not not_1 (not_1_out, in_2);
  and and_2 (out_4, in_1, in_2);
endmodule

module ex4vrai (
  input  in_1,
  output out_2
);

  nand nand_1 (out_2, in_1, in_1);
endmodule
