// Logisim project tp2(1).circ as structural Verilog: 4 circuits, main circuit un_bit
module un_bit (
  input  a,
  input  b,
  output s1,
  output s0
);

  and and_1 (s1, a, b);
  xor xor_1 (s0, a, b);
endmodule

module un_bit_corrige (
  input  A,
  input  B,
  input  c,
  output s1,
  output s0
);

  wire and_1_out, and_2_out, xor_1_out;

  and and_1 (and_1_out, A, B);
  xor xor_1 (xor_1_out, A, B);
  xor xor_2 (s0, xor_1_out, c);
  and and_2 (and_2_out, xor_1_out, c);
  or or_1 (s1, and_1_out, and_2_out);
endmodule

module deux_bit (
  input  [1:0] A,
  input  [1:0] B,
  input  C,
  output S2,
  output S1,
  output S0
);

  wire un_bit_corrige_1_s1;

  un_bit_corrige un_bit_corrige_1 (.A(A[1]), .B(B[1]), .c(C), .s1(un_bit_corrige_1_s1), .s0(S0));
  un_bit_corrige un_bit_corrige_2 (.A(A[0]), .B(B[0]), .c(un_bit_corrige_1_s1), .s1(S2), .s0(S1));
endmodule

module quatre_bit (
  input  [3:0] A,
  input  [3:0] B,
  input  C_entre,
  output [3:0] out_4,
  output C_sortie,
  output S3,
  output S2,
  output S1,
  output s0
);

  wire un_bit_corrige_1_s1, un_bit_corrige_2_s1, un_bit_corrige_3_s1;

  un_bit_corrige un_bit_corrige_1 (.A(A[0]), .B(B[0]), .c(C_entre), .s1(un_bit_corrige_1_s1), .s0(out_4[0]));
  un_bit_corrige un_bit_corrige_2 (
    .A(A[1]), .B(B[1]), .c(un_bit_corrige_1_s1), .s1(un_bit_corrige_2_s1), .s0(out_4[1]));
  un_bit_corrige un_bit_corrige_3 (
    .A(A[2]), .B(B[2]), .c(un_bit_corrige_2_s1), .s1(un_bit_corrige_3_s1), .s0(out_4[2]));
  un_bit_corrige un_bit_corrige_4 (.A(A[3]), .B(B[3]), .c(un_bit_corrige_3_s1), .s1(C_sortie), .s0(out_4[3]));

  assign s0 = out_4[0];
  assign S1 = out_4[1];
  assign S2 = out_4[2];
  assign S3 = out_4[3];
endmodule
