// Logisim project tp3final.circ as structural Verilog
module add1bit (
  input  A,
  input  B,
  input  C,
  output P,
  output G,
  output S
);

  wire xor_1_out;

  xor xor_1 (xor_1_out, A, B);
  xor xor_2 (S, xor_1_out, C);
  or or_1 (P, A, B);
  and and_1 (G, A, B);
endmodule

module unitecalcul (
  input  C0,
  input  P0,
  input  P1,
  input  P2,
  input  P3,
  input  G3,
  input  G2,
  input  G1,
  input  G0,
  output C1,
  output C2,
  output C3,
  output C4,
  output SG,
  output SP
);

  wire and_1_out, and_2_out, and_3_out, and_4_out, and_5_out, and_6_out, and_7_out, and_8_out, and_9_out,
       and_10_out, and_12_out, and_13_out, and_14_out;

  and and_1 (and_1_out, C0, P0);
  or or_1 (C1, and_1_out, G0);
  and and_2 (and_2_out, C0, P0, P1);
  and and_3 (and_3_out, P1, G0);
  or or_2 (C2, and_2_out, and_3_out, G1);
  and and_4 (and_4_out, C0, P0, P1, P2);
  and and_5 (and_5_out, P1, P2, G0);
  or or_3 (C3, and_4_out, and_5_out, and_6_out, G2);
  and and_6 (and_6_out, P2, G1);
  and and_7 (and_7_out, G0, P3, P2, P1, P0);
  and and_8 (and_8_out, G1, P3, P2, P1);
  and and_9 (and_9_out, G2, P2, P3);
  and and_10 (and_10_out, P3, G2);
  or or_4 (C4, and_7_out, and_8_out, and_9_out, and_10_out, G3);
  and and_11 (SP, P0, P1, P2, P3);
  and and_12 (and_12_out, G0, P1, P2, P3);
  and and_13 (and_13_out, G1, P2, P3);
  or or_5 (SG, and_12_out, and_13_out, and_14_out, G3);
  and and_14 (and_14_out, G2, P3);
endmodule

module add4bit (
  input  [3:0] A,
  input  [3:0] B,
  input  C0,
  output C,
  output SG,
  output SP,
  output [3:0] s
);

  wire add1bit_1_g, add1bit_1_p, add1bit_2_g, add1bit_2_p, add1bit_3_g, add1bit_3_p, add1bit_4_g,
       add1bit_4_p, unitecalcul_1_c1, unitecalcul_1_c2, unitecalcul_1_c3;

  add1bit add1bit_1 (.A(A[0]), .B(B[0]), .C(C0), .P(add1bit_1_p), .G(add1bit_1_g), .S(s[0]));
  add1bit add1bit_2 (.A(A[1]), .B(B[1]), .C(unitecalcul_1_c1), .P(add1bit_2_p), .G(add1bit_2_g), .S(s[1]));
  add1bit add1bit_3 (.A(A[2]), .B(B[2]), .C(unitecalcul_1_c2), .P(add1bit_3_p), .G(add1bit_3_g), .S(s[2]));
  add1bit add1bit_4 (.A(A[3]), .B(B[3]), .C(unitecalcul_1_c3), .P(add1bit_4_p), .G(add1bit_4_g), .S(s[3]));
  unitecalcul unitecalcul_1 (
    .C0(C0), .P0(add1bit_1_p), .P1(add1bit_2_p), .P2(add1bit_3_p), .P3(add1bit_4_p), .G3(add1bit_4_g),
    .G2(add1bit_3_g), .G1(add1bit_2_g), .G0(add1bit_1_g), .C1(unitecalcul_1_c1), .C2(unitecalcul_1_c2),
    .C3(unitecalcul_1_c3), .C4(C), .SG(SG), .SP(SP));
endmodule

module ADD16BIT (
  input  in_1,
  input  [15:0] in_2,
  input  [15:0] in_3,
  output out_4,
  output out_5,
  output out_6,
  output [15:0] out_7
);

  wire add4bit_1_sg, add4bit_1_sp, add4bit_2_sg, add4bit_2_sp, add4bit_3_sg, add4bit_3_sp, add4bit_4_sg,
       add4bit_4_sp, unitecalcul_1_c1, unitecalcul_1_c2, unitecalcul_1_c3;

  add4bit add4bit_1 (
    .A(in_2[3:0]), .B(in_3[3:0]), .C0(in_1), .SG(add4bit_1_sg), .SP(add4bit_1_sp), .s(out_7[3:0]));  // open: C
  add4bit add4bit_2 (
    .A(in_2[7:4]), .B(in_3[7:4]), .C0(unitecalcul_1_c1), .SG(add4bit_2_sg), .SP(add4bit_2_sp), .s(out_7[7:4]));  // open: C
  add4bit add4bit_3 (
    .A(in_2[11:8]), .B(in_3[11:8]), .C0(unitecalcul_1_c2), .SG(add4bit_3_sg), .SP(add4bit_3_sp),
    .s(out_7[11:8]));  // open: C
  add4bit add4bit_4 (
    .A(in_2[15:12]), .B(in_3[15:12]), .C0(unitecalcul_1_c3), .SG(add4bit_4_sg), .SP(add4bit_4_sp),
    .s(out_7[15:12]));  // open: C
  unitecalcul unitecalcul_1 (
    .C0(in_1), .P0(add4bit_1_sp), .P1(add4bit_2_sp), .P2(add4bit_3_sp), .P3(add4bit_4_sp), .G3(add4bit_4_sg),
    .G2(add4bit_3_sg), .G1(add4bit_2_sg), .G0(add4bit_1_sg), .C1(unitecalcul_1_c1), .C2(unitecalcul_1_c2),
    .C3(unitecalcul_1_c3), .C4(out_4), .SG(out_5), .SP(out_6));

  // Other names for the same wires on the sheet: C0 = in_1; S[3:0] = out_7[3:0]
endmodule
