// Logisim project partie2.circ as structural Verilog
module unbitcorrige (
  input  in_1,
  input  in_2,
  input  in_3,
  output S1,
  output S0
);

  wire and_1_out, and_2_out, xor_1_out;

  and and_1 (and_1_out, in_1, in_2);
  xor xor_1 (xor_1_out, in_1, in_2);
  xor xor_2 (S0, xor_1_out, in_3);
  and and_2 (and_2_out, xor_1_out, in_3);
  or or_1 (S1, and_1_out, and_2_out);
endmodule

module addi1bit (
  input  in_1,
  input  in_2,
  output out_3,
  output out_4
);

  and and_1 (out_3, in_1, in_2);
  xor xor_1 (out_4, in_1, in_2);
endmodule

module addi4bit (
  input  [3:0] A,
  input  [3:0] B
);

  wire unbitcorrige_1_s1;

  unbitcorrige unbitcorrige_1 (.in_1(A[0]), .in_2(B[0]), .S1(unbitcorrige_1_s1));  // open: in_3, S0
  unbitcorrige unbitcorrige_2 (.in_3(unbitcorrige_1_s1));  // open: in_1, in_2, S1, S0
  unbitcorrige unbitcorrige_3 ();  // open: in_1, in_2, in_3, S1, S0
  unbitcorrige unbitcorrige_4 ();  // open: in_1, in_2, in_3, S1, S0
endmodule
