// Logisim project td2architectureordi.circ as structural Verilog: 3 circuits, main circuit main
module main (
  input  in_1,
  input  in_2,
  input  in_3,
  input  in_4,
  output out_5
);

  wire nand_1_out, nand_2_out;

  nand nand_1 (nand_1_out, in_1, in_2);
  nand nand_2 (nand_2_out, in_3, in_4);
  nand nand_3 (out_5, nand_1_out, nand_2_out);
endmodule

module basculejk (
  input  in_1,
  input  in_2,
  input  in_3
);

  // AND_Gate and_1 is placed but not wired
  // OR_Gate or_1 is placed but not wired
endmodule

module verroud (
  input  in_1,
  input  in_2,
  input  in_3,
  output out_4,
  output out_5,
  output out_6,
  output out_7
);

  wire nand_1_out, nand_2_out, nand_3_out, nand_4_out, not_1_out, not_2_out, not_3_out;

  not not_1 (not_1_out, in_2);
  not not_2 (not_2_out, in_1);
  not not_3 (not_3_out, in_3);
  nand nand_1 (nand_1_out, in_1, in_2);
  nand nand_2 (nand_2_out, in_2, not_2_out);
  nand nand_3 (nand_3_out, in_3, not_1_out);
  nand nand_4 (nand_4_out, not_1_out, not_3_out);
  nand nand_5 (out_4, out_5, nand_1_out);
  nand nand_6 (out_5, nand_2_out, out_4);
  nand nand_7 (out_6, out_7, nand_3_out);
  nand nand_8 (out_7, nand_4_out, out_6);
endmodule
